// Logisim project 74Logic.circ as structural Verilog: 4 circuits, main circuit SN74LS01
module SN74LS01 (
  input  A1,
  input  B1,
  input  A2,
  input  B2,
  input  A3,
  input  B3,
  input  A4,
  input  B4,
  output Y1,
  output Y2,
  output Y3,
  output Y4
);

  wire and_1_out, and_2_out, and_3_out, and_4_out;

  and and_1 (and_1_out, A1, B1);
  and and_2 (and_2_out, A2, B2);
  and and_3 (and_3_out, A3, B3);
  and and_4 (and_4_out, A4, B4);
  assign Y1 = and_1_out ? 1'b0 : 1'bz;  // Controlled_Buffer controlled_buffer_1
  assign Y2 = and_2_out ? 1'b0 : 1'bz;  // Controlled_Buffer controlled_buffer_2
  assign Y3 = and_3_out ? 1'b0 : 1'bz;  // Controlled_Buffer controlled_buffer_3
  assign Y4 = and_4_out ? 1'b0 : 1'bz;  // Controlled_Buffer controlled_buffer_4
endmodule

module SN74LS03 (
  input  A1,
  input  B1,
  input  A2,
  input  B2,
  input  A3,
  input  B3,
  input  A4,
  input  B4,
  output Y1,
  output Y2,
  output Y3,
  output Y4
);

  wire and_1_out, and_2_out, and_3_out, and_4_out;

  and and_1 (and_1_out, A1, B1);
  and and_2 (and_2_out, A2, B2);
  and and_3 (and_3_out, A3, B3);
  and and_4 (and_4_out, A4, B4);
  assign Y1 = and_1_out ? 1'b0 : 1'bz;  // Controlled_Buffer controlled_buffer_1
  assign Y2 = and_2_out ? 1'b0 : 1'bz;  // Controlled_Buffer controlled_buffer_2
  assign Y3 = and_3_out ? 1'b0 : 1'bz;  // Controlled_Buffer controlled_buffer_3
  assign Y4 = and_4_out ? 1'b0 : 1'bz;  // Controlled_Buffer controlled_buffer_4
endmodule

module SN74LS05 (
  input  A1,
  input  A2,
  input  A3,
  input  A4,
  input  A5,
  input  A6,
  output Y1,
  output Y2,
  output Y3,
  output Y4,
  output Y5,
  output Y6
);

  assign Y1 = A1 ? 1'b0 : 1'bz;  // Controlled_Buffer controlled_buffer_1
  assign Y2 = A2 ? 1'b0 : 1'bz;  // Controlled_Buffer controlled_buffer_2
  assign Y3 = A3 ? 1'b0 : 1'bz;  // Controlled_Buffer controlled_buffer_3
  assign Y4 = A4 ? 1'b0 : 1'bz;  // Controlled_Buffer controlled_buffer_4
  assign Y5 = A5 ? 1'b0 : 1'bz;  // Controlled_Buffer controlled_buffer_5
  assign Y6 = A6 ? 1'b0 : 1'bz;  // Controlled_Buffer controlled_buffer_6
endmodule

module SN74LS06 (
  input  A1,
  input  A2,
  input  A3,
  input  A4,
  input  A5,
  input  A6,
  output Y1,
  output Y2,
  output Y3,
  output Y4,
  output Y5,
  output Y6
);

  assign Y1 = A1 ? 1'b0 : 1'bz;  // Controlled_Buffer controlled_buffer_1
  assign Y2 = A2 ? 1'b0 : 1'bz;  // Controlled_Buffer controlled_buffer_2
  assign Y3 = A3 ? 1'b0 : 1'bz;  // Controlled_Buffer controlled_buffer_3
  assign Y4 = A4 ? 1'b0 : 1'bz;  // Controlled_Buffer controlled_buffer_4
  assign Y5 = A5 ? 1'b0 : 1'bz;  // Controlled_Buffer controlled_buffer_5
  assign Y6 = A6 ? 1'b0 : 1'bz;  // Controlled_Buffer controlled_buffer_6
endmodule
